# Fritzing sketch hardware-layout (saved by Fritzing 0.9.10b)
breadboards: 1

parts:
  Raspberry_Pi_1 = Raspberry Pi 4 [part_number=RPI-4-b]
  SP1 = SPEAKER [package=pcb_mount_speaker]
  R1 = Resistor [tolerance=±5% resistance=100 package="0805 [SMD]"]
  SEN1 = US-100 Ultrasonic Distance Sensor
  A1 = GY-NEO6MV2
  R4 = Resistor [tolerance=±5% resistance=10k package="0603 [SMD]"]
  R5 = Resistor [tolerance=±5% resistance=10k package="0603 [SMD]"]

nets:
  GND: Raspberry_Pi_1.GND, SP1.+, SEN1.GND, SEN1.GND-2, A1.Tx, R5.Pin_0
  N1: Raspberry_Pi_1.GPIO12, R1.Pin_0
  N2: Raspberry_Pi_1.GPIO24, R4.Pin_0, R5.Pin_1
  N3: Raspberry_Pi_1.GPIO23, SEN1.TRIG
  N4: Raspberry_Pi_1.GPIO15, A1.Rx
  N5: Raspberry_Pi_1.GPIO14, A1.Vcc#1
  5V: Raspberry_Pi_1.5V, SEN1.VCC, A1.Vcc#0
  N6: SP1.-, R1.Pin_1
  N7: SEN1.ECHO, R4.Pin_1

custom parts:
  Raspberry Pi 4: The RPi4, a faster version of the awesome Raspberry Pi 2 B ARM Board with 40 pin gpio. Ready for special Raspberry Pi B+ and RPi2 Hat (Hardware attached (on) top)
  GY-NEO6MV2: Description: Module GPS , type GY-NEO6MV2, pour arduino et autres micro-contrôleurs. Caractéristiques De type GY-NEO6MV2 Alimentation 3V-5V Avec Flight Control EEPROM MWC Antenne large céramique, fort signal, 25 x 25 mm Paramètres de configuration sauvegardés en EEPROM Avec batterie de backup de données LED témoin de signal Module miniaturisé 25 x 35 mm Trou de fixation de 3mm Baud rate par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
